// Logisim project s-mips.circ as structural Verilog
module S_MIPS_Board (
  input  DESHABILITAR_DISPATCHER,
  output halt
);

  wire button_1_out, CLK, CS, d_ff_1_q, LCLR, LoadRAM, LoadRAMOn, LW, R_R_W, R_W, ram_dispatcher_1_finished,
       RCS, Reset_out, RST, TTY_EN;
  wire [2:0] KDB;
  wire [3:0] LMask, Mask, ram_1_read_time, ram_1_write_time, RMask;
  wire [6:0] KDB_DATA, TTY_DATA;
  wire [15:0] Addr, LAddr, RAddr;
  wire [31:0] I0, I1, I2, I3, LData, ram_1_data_out_0, ram_1_data_out_1, ram_1_data_out_2, ram_1_data_out_3,
       RI0, RI1, RI2, RI3;

  TTY #(.rows(25), .cols(80)) tty_1 (.data(TTY_DATA), .clk(CLK), .we(TTY_EN), .clr(RST));
  not not_1 (LoadRAMOn, ram_dispatcher_1_finished);
  RAM_Dispatcher ram_dispatcher_1 (
    .WriteTime(ram_1_write_time), .Clock(CLK), .Data(LData), .Address(LAddr), .Mask(LMask),
    .Finished(ram_dispatcher_1_finished), .Write(LW), .CLR(LCLR));
  Keyboard #(.buflen(64)) keyboard_1 (.clk(CLK), .re(KDB[0]), .avail(KDB[2]), .data(KDB_DATA));  // open: clr
  RAM ram_1 (
    .Address(RAddr), .Data_Out_0(ram_1_data_out_0), .Data_Out_1(ram_1_data_out_1),
    .Data_Out_2(ram_1_data_out_2), .Data_Out_3(ram_1_data_out_3), .Data_In_0(RI0), .Data_In_1(RI1),
    .Data_In_2(RI2), .Data_In_3(RI3), .Mask(RMask), .nRead_Write(R_R_W), .Chip_Select(RCS),
    .Read_Time(ram_1_read_time), .Reset(button_1_out), .Write_Time(ram_1_write_time));
  Button button_1 (.out(button_1_out));
  D_Flip_Flop d_ff_1 (.clk(CLK), .D(1'b1), .Q(d_ff_1_q), .reset(Reset_out));  // open: Qn, preset, en
  Button Reset (.out(Reset_out));
  S_MIPS s_mips_1 (
    .Kbd_Enable(KDB[0]), .Address(Addr), .Kbd_Clear(KDB[1]), .Kbd_Available(KDB[2]), .RAM_In_0(I0),
    .Kbd_ASCII_Data(KDB_DATA), .RAM_In_1(I1), .TTY_Enable(TTY_EN), .RAM_In_2(I2), .RAM_In_3(I3),
    .TTY_ASCII_Data(TTY_DATA), .Reset(RST), .RAM_Out_0(ram_1_data_out_0), .Clock(CLK),
    .RAM_Out_1(ram_1_data_out_1), .Stop(halt), .RAM_Out_2(ram_1_data_out_2), .RAM_Out_3(ram_1_data_out_3),
    .Mask(Mask), .Read_Time(ram_1_read_time), .Write_Time(ram_1_write_time), .nRead_Write(R_W),
    .Chip_Select(CS));
  D_Flip_Flop d_ff_2 (.clk(CLK), .D(d_ff_1_q), .Qn(LCLR), .reset(Reset_out));  // open: Q, preset, en
  or or_1 (RST, LCLR, LoadRAM);
  Clock clock_1 (.out(CLK));
  Multiplexer #(.width(32), .enable("false")) multiplexer_1 (.in0(I0), .in1(LData), .out(RI0), .sel(LoadRAM));
  Multiplexer #(.width(32), .enable("false")) multiplexer_2 (.in0(I1), .in1(LData), .out(RI1), .sel(LoadRAM));
  Multiplexer #(.width(32), .enable("false")) multiplexer_3 (.in0(I2), .in1(LData), .out(RI2), .sel(LoadRAM));
  Multiplexer #(.width(32), .enable("false")) multiplexer_4 (.in0(I3), .in1(LData), .out(RI3), .sel(LoadRAM));
  and and_1 (LoadRAM, ~DESHABILITAR_DISPATCHER, LoadRAMOn);  // AND_Gate
  Multiplexer #(.width(16), .enable("false")) multiplexer_5 (.in0(Addr), .in1(LAddr), .out(RAddr), .sel(LoadRAM));
  Multiplexer #(.width(4), .enable("false")) multiplexer_6 (.in0(Mask), .in1(LMask), .out(RMask), .sel(LoadRAM));
  Multiplexer #(.enable("false")) multiplexer_7 (.in0(CS), .in1(LW), .out(RCS), .sel(LoadRAM));
  Multiplexer #(.enable("false")) multiplexer_8 (.in0(R_W), .in1(LW), .out(R_R_W), .sel(LoadRAM));

  // Notes on the sheet:
  //   NO MODIFICAR
  //   Keyboard
endmodule

module RAM (
  input  [15:0] Address,
  input  [31:0] Data_In_0,
  input  [31:0] Data_In_1,
  input  [31:0] Data_In_2,
  input  [31:0] Data_In_3,
  input  [3:0] Mask,
  input  nRead_Write,
  input  Chip_Select,
  input  Reset,
  output [31:0] Data_Out_0,
  output [31:0] Data_Out_1,
  output [31:0] Data_Out_2,
  output [31:0] Data_Out_3,
  output [3:0] Read_Time,
  output [3:0] Write_Time
);

  wire and_2_out, and_3_out, and_4_out, and_5_out, and_6_out, and_7_out, and_8_out, and_9_out, Changed, CLK,
       comparator_2_eq, comparator_3_eq, comparator_4_eq, comparator_5_eq, comparator_6_eq, Count,
       demultiplexer_3_out0, Idle, Idle_q, Load, Load0, Load1, nand_1_out, or_1_out, or_2_out, or_3_out,
       or_4_out, or_5_out, or_6_out, or_7_out, or_8_out, or_9_out, or_10_out, Proc_q, Update_Mem, Zero_Time;
  wire [3:0] counter_1_q, multiplexer_1_out, subtractor_1_out;
  wire [31:0] register_1_q, register_2_q, register_3_q, register_4_q, register_5_q;

  // Probe on 4'b0011
  // Probe on 4'b0010
  Multiplexer #(.width(4), .enable("false")) multiplexer_1 (
    .in0(4'b0011), .in1(4'b0010), .out(multiplexer_1_out), .sel(nRead_Write));
  or or_1 (or_1_out, Idle, Update_Mem);
  or or_2 (or_2_out, ~Chip_Select, Reset);  // OR_Gate
  Subtractor #(.width(4)) subtractor_1 (.a(multiplexer_1_out), .b(4'b0010), .out(subtractor_1_out));  // open: bin, bout
  Demultiplexer #(.enable("false")) demultiplexer_1 (.out0(Idle), .out1(Load0), .in(Idle_q), .sel(Changed));
  D_Flip_Flop u_Idle (.clk(CLK), .D(or_1_out), .Q(Idle_q), .preset(or_2_out));  // open: Qn, en, reset
  // Probe on counter_1_q
  Counter #(.width(4), .max('hf)) counter_1 (
    .load(Load), .D(subtractor_1_out), .count(Count), .Q(counter_1_q), .clk(CLK), .clr(or_3_out));  // open: carry
  or or_3 (or_3_out, ~Chip_Select, Reset);  // OR_Gate
  Comparator #(.width(4), .mode("unsigned")) comparator_1 (
    .a(4'b0000), .b(counter_1_q), .eq(Zero_Time));  // open: gt, lt
  or or_4 (or_4_out, Count, Load0, Load1);
  Register #(.width(32)) register_1 (.D(Data_In_0), .en(Chip_Select), .Q(register_1_q), .clk(CLK), .clr(or_5_out));
  or or_5 (or_5_out, ~Chip_Select, Reset);  // OR_Gate
  Register #(.width(32)) register_2 (.D(Data_In_1), .en(Chip_Select), .Q(register_2_q), .clk(CLK), .clr(or_6_out));
  or or_6 (or_6_out, ~Chip_Select, Reset);  // OR_Gate
  Register #(.width(32)) register_3 (.D(Data_In_2), .en(Chip_Select), .Q(register_3_q), .clk(CLK), .clr(or_7_out));
  or or_7 (or_7_out, ~Chip_Select, Reset);  // OR_Gate
  Register #(.width(32)) register_4 (.D(Data_In_3), .en(Chip_Select), .Q(register_4_q), .clk(CLK), .clr(or_8_out));
  or or_8 (or_8_out, ~Chip_Select, Reset);  // OR_Gate
  Register #(.width(32)) register_5 (
    .D({{11{1'b1}}, nRead_Write, Mask, Address}), .en(Chip_Select), .Q(register_5_q), .clk(CLK),
    .clr(or_9_out));
  or or_9 (or_9_out, ~Chip_Select, Reset);  // OR_Gate
  D_Flip_Flop Proc (.clk(CLK), .D(or_4_out), .Q(Proc_q), .reset(or_10_out));  // open: Qn, preset, en
  or or_10 (or_10_out, ~Chip_Select, Reset);  // OR_Gate
  Demultiplexer #(.enable("false")) demultiplexer_2 (
    .out0(Count), .out1(Update_Mem), .in(demultiplexer_3_out0), .sel(Zero_Time));
  Demultiplexer #(.enable("false")) demultiplexer_3 (
    .out0(demultiplexer_3_out0), .out1(Load1), .in(Proc_q), .sel(Changed));
  Clock clock_1 (.out(CLK));
  Comparator #(.width(32)) comparator_2 (.a(register_1_q), .b(Data_In_0), .eq(comparator_2_eq));  // open: gt, lt
  Comparator #(.width(32)) comparator_3 (.a(register_2_q), .b(Data_In_1), .eq(comparator_3_eq));  // open: gt, lt
  Comparator #(.width(32)) comparator_4 (.a(register_3_q), .b(Data_In_2), .eq(comparator_4_eq));  // open: gt, lt
  Comparator #(.width(32)) comparator_5 (.a(register_4_q), .b(Data_In_3), .eq(comparator_5_eq));  // open: gt, lt
  Comparator #(.width(32)) comparator_6 (
    .a(register_5_q), .b({{11{1'b1}}, nRead_Write, Mask, Address}), .eq(comparator_6_eq));  // open: gt, lt
  nand nand_1 (nand_1_out, comparator_6_eq, comparator_2_eq, comparator_3_eq, comparator_4_eq, comparator_5_eq);
  and and_1 (Changed, nand_1_out, Chip_Select);
  or or_11 (Load, Count, Load1, Load0);
  and and_2 (and_2_out, Mask[0], Update_Mem, nRead_Write);
  and and_3 (and_3_out, Mask[1], Update_Mem, nRead_Write);
  and and_4 (and_4_out, Mask[2], Update_Mem, nRead_Write);
  and and_5 (and_5_out, Mask[3], Update_Mem, nRead_Write);
  RAM_part #(.addrWidth(16), .dataWidth(32), .bus("separate")) ram_1 (
    .addr(Address), .din(Data_In_0), .data(Data_Out_0), .str(and_2_out), .sel(Chip_Select), .clk(CLK),
    .ld(and_6_out), .clr(Reset));
  and and_6 (and_6_out, ~nRead_Write, Idle);  // AND_Gate
  RAM_part #(.addrWidth(16), .dataWidth(32), .bus("separate")) ram_2 (
    .addr(Address), .din(Data_In_1), .data(Data_Out_1), .str(and_3_out), .sel(Chip_Select), .clk(CLK),
    .ld(and_7_out), .clr(Reset));
  and and_7 (and_7_out, ~nRead_Write, Idle);  // AND_Gate
  RAM_part #(.addrWidth(16), .dataWidth(32), .bus("separate")) ram_3 (
    .addr(Address), .din(Data_In_2), .data(Data_Out_2), .str(and_4_out), .sel(Chip_Select), .clk(CLK),
    .ld(and_8_out), .clr(Reset));
  and and_8 (and_8_out, ~nRead_Write, Idle);  // AND_Gate
  RAM_part #(.addrWidth(16), .dataWidth(32), .bus("separate")) ram_4 (
    .addr(Address), .din(Data_In_3), .data(Data_Out_3), .str(and_5_out), .sel(Chip_Select), .clk(CLK),
    .ld(and_9_out), .clr(Reset));
  and and_9 (and_9_out, ~nRead_Write, Idle);  // AND_Gate

  assign Read_Time = 4'b0011;
  assign Write_Time = 4'b0010;

  // Other names for the same wires on the sheet: M0 = Mask[0]; M1 = Mask[1]; M2 = Mask[2]; M3 = Mask[3];
  //   RW = nRead_Write; CLR = Reset; CS = Chip_Select; Load2 = Count

  // Notes on the sheet:
  //   NO MODIFICAR
  //   excepto quizás los valores RT y WT
  //   BANK0
  //   BANK1
  //   BANK2
  //   BANK3
endmodule

module S_MIPS (
  input  Kbd_Available,
  input  [6:0] Kbd_ASCII_Data,
  input  [31:0] RAM_Out_0,
  input  [31:0] RAM_Out_1,
  input  Reset,
  input  [31:0] RAM_Out_2,
  input  Clock,
  input  [31:0] RAM_Out_3,
  input  [3:0] Read_Time,
  input  [3:0] Write_Time,
  output Kbd_Enable,
  output [15:0] Address,
  output Kbd_Clear,
  output TTY_Enable,
  output [6:0] TTY_ASCII_Data,
  output Stop,
  output [31:0] RAM_In_0,
  output [31:0] RAM_In_1,
  output [31:0] RAM_In_2,
  output [31:0] RAM_In_3,
  output [3:0] Mask,
  output nRead_Write,
  output Chip_Select
);


  // Other names for the same wires on the sheet: CLK = Clock; CLR = Reset; CS = Chip_Select;
  //   KBD_AVAIL = Kbd_Available; KBD_CLR = Kbd_Clear; KBD_DATA[6:0] = Kbd_ASCII_Data; RAM_A[15:0] = Address;
  //   RAM_INPUT_0[31:0] = RAM_In_0; RAM_INPUT_1[31:0] = RAM_In_1; RAM_INPUT_2[31:0] = RAM_In_2;
  //   RAM_INPUT_3[31:0] = RAM_In_3; RAM_MASK[3:0] = Mask; RAM_OUTPUT_0[31:0] = RAM_Out_0;
  //   RAM_OUTPUT_1[31:0] = RAM_Out_1; RAM_OUTPUT_2[31:0] = RAM_Out_2; RAM_OUTPUT_3[31:0] = RAM_Out_3;
  //   RW = nRead_Write; TTY_DATA[6:0] = TTY_ASCII_Data

  // Notes on the sheet:
  //   RAM ADDRESS
  //   DATA FROM RAM
  //   DATA TO RAM
  //   DATA WRITE MASK
  //   RAM TIMING
  //   RAM CONTROL
  //   KEYBOARD
  //   TTY
  //   SEQUENCING
endmodule

module RAM_Dispatcher (
  input  [3:0] WriteTime,
  input  Clock,
  input  CLR,
  output [31:0] Data,
  output [15:0] Address,
  output [3:0] Mask,
  output Finished,
  output Write
);

  wire demultiplexer_2_out1, demultiplexer_3_out1, End, IDLE_q, IncAddr, Load, or_1_out, or_2_out, While_q,
       WriteEnd;
  wire [3:0] counter_1_q;
  wire [31:0] CurrentAddress_q;

  Counter #(.width(32), .max('hffffffff)) CurrentAddress (
    .count(IncAddr), .Q({CurrentAddress_q[31:18], Address, CurrentAddress_q[1:0]}), .clk(Clock), .clr(CLR));  // open: load, D, carry
  or or_1 (or_1_out, IncAddr, demultiplexer_3_out1, Finished);
  D_Flip_Flop IDLE (.clk(Clock), .D(or_1_out), .Q(IDLE_q), .preset(CLR));  // open: Qn, en, reset
  Demultiplexer #(.enable("false")) demultiplexer_1 (.out0(Load), .out1(Finished), .in(IDLE_q), .sel(End));
  D_Flip_Flop While (.clk(Clock), .D(or_2_out), .Q(While_q), .reset(CLR));  // open: Qn, preset, en
  or or_2 (or_2_out, Write, Load);
  RAM_part #(.addrWidth(18), .dataWidth(32)) ram_1 (
    .addr({Address, CurrentAddress_q[1:0]}), .data(Data), .clk(Clock));  // open: sel, ld, clr
  Demultiplexer #(.enable("false")) demultiplexer_2 (
    .out0(Write), .out1(demultiplexer_2_out1), .in(While_q), .sel(WriteEnd));
  Decoder #(.select(2)) decoder_1 (
    .out0(Mask[0]), .out1(Mask[1]), .out2(Mask[2]), .out3(Mask[3]), .sel(CurrentAddress_q[1:0]));  // open: en
  Demultiplexer #(.enable("false")) demultiplexer_3 (
    .out0(IncAddr), .out1(demultiplexer_3_out1), .in(demultiplexer_2_out1), .sel(End));
  Counter #(.width(4), .max('hf)) counter_1 (
    .load(Load), .D(WriteTime), .count(Write), .Q(counter_1_q), .clk(Clock));  // open: carry, clr
  Comparator #(.width(32)) comparator_1 (.a(Data), .b({32{1'b1}}), .eq(End));  // open: gt, lt
  Comparator #(.width(4)) comparator_2 (.a(4'b0000), .b(counter_1_q), .eq(WriteEnd));  // open: gt, lt

  // Other names for the same wires on the sheet: CLK = Clock; Count = Write; WT[3:0] = WriteTime
endmodule

module Register_File (
  input  [4:0] DA,
  input  [31:0] DI,
  input  R_W,
  input  [4:0] SA,
  input  [4:0] SB,
  input  Clk,
  input  Reset,
  input  [31:0] Hi,
  input  [31:0] Lo,
  input  R_W_Hi_Lo,
  output [31:0] Data_A,
  output [31:0] Data_B,
  output [31:0] SP,
  output [31:0] Hi_Out,
  output [31:0] Lo_Out
);

  wire R0, R1, R2, R3, R4, R5, R6, R7, R8, R9, R10, R11, R12, R13, R14, R15, R16, R17, R18, R19, R20, R21,
       R22, R23, R24, R25, R26, R27, R28, R29, R30, SP_t;
  wire [31:0] R0_Out, R1_Out, R2_Out, R3_Out, R4_Out, R5_Out, R6_Out, R7_Out, R8_Out, R9_Out, R10_Out,
       R11_Out, R12_Out, R13_Out, R14_Out, R15_Out, R16_Out, R17_Out, R18_Out, R19_Out, R20_Out, R21_Out,
       R22_Out, R23_Out, R24_Out, R25_Out, R26_Out, R27_Out, R28_Out, R29_Out, R30_Out;

  Decoder #(.select(5), .disabled(0)) decoder_1 (
    .out0(R0), .out1(R1), .out2(R2), .out3(R3), .out4(R4), .out5(R5), .out6(R6), .out7(R7), .out8(R8),
    .out9(R9), .out10(R10), .out11(R11), .out12(R12), .out13(R13), .out14(R14), .out15(R15), .out16(R16),
    .out17(R17), .out18(R18), .out19(R19), .out20(R20), .out21(R21), .out22(R22), .out23(R23), .out24(R24),
    .out25(R25), .out26(R26), .out27(R27), .out28(R28), .out29(R29), .out30(R30), .out31(SP_t), .sel(DA),
    .en(R_W));
  Register #(.width(32)) u_R0 (.D({32{1'b0}}), .en(R0), .Q(R0_Out), .clk(Clk), .clr(Reset));
  Register #(.width(32)) u_R4 (.D(DI), .en(R4), .Q(R4_Out), .clk(Clk), .clr(Reset));
  Register #(.width(32)) u_R8 (.D(DI), .en(R8), .Q(R8_Out), .clk(Clk), .clr(Reset));
  Register #(.width(32)) u_R12 (.D(DI), .en(R12), .Q(R12_Out), .clk(Clk), .clr(Reset));
  Register #(.width(32)) u_R16 (.D(DI), .en(R16), .Q(R16_Out), .clk(Clk), .clr(Reset));
  Register #(.width(32)) u_R20 (.D(DI), .en(R20), .Q(R20_Out), .clk(Clk), .clr(Reset));
  Register #(.width(32)) u_R24 (.D(DI), .en(R24), .Q(R24_Out), .clk(Clk), .clr(Reset));
  Register #(.width(32)) u_R28 (.D(DI), .en(R28), .Q(R28_Out), .clk(Clk), .clr(Reset));
  Register #(.width(32)) u_R25 (.D(DI), .en(R25), .Q(R25_Out), .clk(Clk), .clr(Reset));
  Register #(.width(32)) u_R29 (.D(DI), .en(R29), .Q(R29_Out), .clk(Clk), .clr(Reset));
  Multiplexer #(.select(5), .width(32), .enable("false")) multiplexer_1 (
    .in0(R0_Out), .in1(R1_Out), .in2(R2_Out), .in3(R3_Out), .in4(R4_Out), .in5(R5_Out), .in6(R6_Out),
    .in7(R7_Out), .in8(R8_Out), .in9(R9_Out), .in10(R10_Out), .in11(R11_Out), .in12(R12_Out), .in13(R13_Out),
    .in14(R14_Out), .in15(R15_Out), .in16(R16_Out), .in17(R17_Out), .in18(R18_Out), .in19(R19_Out),
    .in20(R20_Out), .in21(R21_Out), .in22(R22_Out), .in23(R23_Out), .in24(R24_Out), .in25(R25_Out),
    .in26(R26_Out), .in27(R27_Out), .in28(R28_Out), .in29(R29_Out), .in30(R30_Out), .in31(SP), .out(Data_A),
    .sel(SA));
  Register #(.width(32)) u_R1 (.D(DI), .en(R1), .Q(R1_Out), .clk(Clk), .clr(Reset));
  Register #(.width(32)) u_R5 (.D(DI), .en(R5), .Q(R5_Out), .clk(Clk), .clr(Reset));
  Register #(.width(32)) u_R9 (.D(DI), .en(R9), .Q(R9_Out), .clk(Clk), .clr(Reset));
  Register #(.width(32)) u_R13 (.D(DI), .en(R13), .Q(R13_Out), .clk(Clk), .clr(Reset));
  Register #(.width(32)) u_R17 (.D(DI), .en(R17), .Q(R17_Out), .clk(Clk), .clr(Reset));
  Register #(.width(32)) u_R21 (.D(DI), .en(R21), .Q(R21_Out), .clk(Clk), .clr(Reset));
  Register #(.width(32)) u_R2 (.D(DI), .en(R2), .Q(R2_Out), .clk(Clk), .clr(Reset));
  Register #(.width(32)) u_R6 (.D(DI), .en(R6), .Q(R6_Out), .clk(Clk), .clr(Reset));
  Register #(.width(32)) u_R10 (.D(DI), .en(R10), .Q(R10_Out), .clk(Clk), .clr(Reset));
  Register #(.width(32)) u_R14 (.D(DI), .en(R14), .Q(R6_Out), .clk(Clk), .clr(Reset));
  Register #(.width(32)) u_R18 (.D(DI), .en(R18), .Q(R18_Out), .clk(Clk), .clr(Reset));
  Register #(.width(32)) u_R22 (.D(DI), .en(R22), .Q(R22_Out), .clk(Clk), .clr(Reset));
  Register #(.width(32)) u_R26 (.D(DI), .en(R26), .Q(R26_Out), .clk(Clk), .clr(Reset));
  Register #(.width(32)) u_R30 (.D(DI), .en(R30), .Q(R30_Out), .clk(Clk), .clr(Reset));
  Register #(.width(32)) u_R3 (.D(DI), .en(R3), .Q(R3_Out), .clk(Clk), .clr(Reset));
  Register #(.width(32)) u_R7 (.D(DI), .en(R7), .Q(R7_Out), .clk(Clk), .clr(Reset));
  Register #(.width(32)) u_R11 (.D(DI), .en(R11), .Q(R11_Out), .clk(Clk), .clr(Reset));
  Register #(.width(32)) u_R15 (.D(DI), .en(R15), .Q(R15_Out), .clk(Clk), .clr(Reset));
  Register #(.width(32)) u_R19 (.D(DI), .en(R19), .Q(R19_Out), .clk(Clk), .clr(Reset));
  Register #(.width(32)) u_R23 (.D(DI), .en(R23), .Q(R23_Out), .clk(Clk), .clr(Reset));
  Register #(.width(32)) u_R27 (.D(DI), .en(R27), .Q(R27_Out), .clk(Clk), .clr(Reset));
  Register #(.width(32)) u_SP (.D(DI), .en(SP_t), .Q(SP), .clk(Clk), .clr(Reset));
  Multiplexer #(.select(5), .width(32), .enable("false")) multiplexer_2 (
    .in0(R0_Out), .in1(R1_Out), .in2(R2_Out), .in3(R3_Out), .in4(R4_Out), .in5(R5_Out), .in6(R6_Out),
    .in7(R7_Out), .in8(R8_Out), .in9(R9_Out), .in10(R10_Out), .in11(R11_Out), .in12(R12_Out), .in13(R13_Out),
    .in14(R14_Out), .in15(R15_Out), .in16(R16_Out), .in17(R17_Out), .in18(R18_Out), .in19(R19_Out),
    .in20(R20_Out), .in21(R21_Out), .in22(R22_Out), .in23(R23_Out), .in24(R24_Out), .in25(R25_Out),
    .in26(R26_Out), .in27(R27_Out), .in28(R28_Out), .in29(R29_Out), .in30(R30_Out), .in31(SP), .out(Data_B),
    .sel(SB));
  Register #(.width(32)) u_Hi (.D(Hi), .en(R_W_Hi_Lo), .Q(Hi_Out), .clk(Clk), .clr(Reset));
  Register #(.width(32)) u_Lo (.D(Lo), .en(R_W_Hi_Lo), .Q(Lo_Out), .clk(Clk), .clr(Reset));

  // Other names for the same wires on the sheet: Rst = Reset; RW = R_W; RWHL = R_W_Hi_Lo; SP_Out[31:0] = SP

  // Notes on the sheet:
  //   Data Adress
  //   Data In
  //   Read/Write
  //   Selector A
  //   Selector B
  //   Inputs
  //   Write
  //   Registers
  //   Read
  //   Outputs
  //   Hi-Lo Registers
endmodule

module Conversor_de_entrada (
  input  [31:0] in_1,
  output [31:0] Output
);

  wire [31:0] B;

  assign B = ~in_1;  // NOT_Gate not_1, 32 bits wide
  Adder #(.width(32)) adder_1 (.a(B), .b(32'h1), .out(Output));  // open: cin, cout

  // Other names for the same wires on the sheet: A[31:0] = in_1
endmodule

module Convensor_de_salida (
  input  [31:0] in_1,
  output [31:0] Output
);

  wire [31:0] subtractor_1_out;

  Subtractor #(.width(32)) subtractor_1 (.a(in_1), .b(32'h1), .out(subtractor_1_out));  // open: bin, bout
  assign Output = ~subtractor_1_out;  // NOT_Gate not_1, 32 bits wide

  // Other names for the same wires on the sheet: A[31:0] = in_1
endmodule

module Conversor_de_mult_div (
  input  [31:0] Hy,
  input  [31:0] Lo,
  output [31:0] Output_Hy,
  output [31:0] Output_Lo
);

  wire subtractor_1_bout;
  wire [31:0] subtractor_1_out, subtractor_2_out;

  Subtractor #(.width(32)) subtractor_1 (
    .a(Hy), .b(32'h1), .out(subtractor_1_out), .bout(subtractor_1_bout));  // open: bin
  assign Output_Hy = ~subtractor_1_out;  // NOT_Gate not_1, 32 bits wide
  assign Output_Lo = ~subtractor_2_out;  // NOT_Gate not_2, 32 bits wide
  Subtractor #(.width(32)) subtractor_2 (
    .a(Lo), .b({32{1'b0}}), .out(subtractor_2_out), .bin(subtractor_1_bout));  // open: bout

  // Other names for the same wires on the sheet: A[31:0] = Hy; B[31:0] = Lo
endmodule

module ALU (
  input  [31:0] in_1,
  input  [31:0] in_2,
  input  [3:0] in_3,
  output Cero,
  output Negative,
  output [31:0] Output,
  output [31:0] Output_Hi
);

  wire comparator_1_eq, comparator_1_lt;
  wire [31:0] Add, And, C_Div, C_mult, Div, Equal, Mult, Nor, Or, Slt, Sub, Xor;

  Adder #(.width(32)) adder_1 (.a(in_1), .b(in_2), .out(Add));  // open: cin, cout
  Subtractor #(.width(32)) subtractor_1 (.a(in_1), .b(in_2), .out(Sub));  // open: bin, bout
  Comparator #(.width(32)) comparator_1 (.a(in_1), .b(in_2), .eq(comparator_1_eq), .lt(comparator_1_lt));  // open: gt
  Multiplexer #(.width(32), .enable("false")) multiplexer_1 (
    .in0(32'h1), .in1({32{1'b0}}), .out(Slt), .sel(comparator_1_lt));
  Multiplier #(.width(32)) multiplier_1 (.a(in_1), .b(in_2), .out(Mult), .cout(C_mult));  // open: cin
  Divider #(.width(32)) divider_1 (.a(in_1), .b(in_2), .out(Div), .rem(C_Div));  // open: upper
  assign Equal = {{31{1'b0}}, comparator_1_eq};  // Bit_Extender bit_extender_1
  assign And = in_1 & in_2;  // AND_Gate and_1, 32 bits wide
  assign Or = in_1 | in_2;  // OR_Gate or_1, 32 bits wide
  assign Nor = ~(in_1 | in_2);  // NOR_Gate nor_1, 32 bits wide
  assign Xor = in_1 ^ in_2;  // XOR_Gate xor_1, 32 bits wide
  Multiplexer #(.width(32), .enable("false")) multiplexer_2 (.in0(C_mult), .in1(C_Div), .out(Output_Hi), .sel(in_3[0]));
  Comparator #(.width(32)) comparator_2 (.a(Output), .b({32{1'b0}}), .eq(Cero), .lt(Negative));  // open: gt
  Multiplexer #(.select(4), .width(32), .enable("false")) multiplexer_3 (
    .in0(Add), .in1(Sub), .in2(Mult), .in3(Div), .in4(Slt), .in5(And), .in6(Or), .in7(Nor), .in8(Xor),
    .in15(Equal), .out(Output), .sel(in_3));  // open: in9, in10, in11, in12, in13, in14

  // Other names for the same wires on the sheet: A[31:0] = in_1; B[31:0] = in_2; Result[31:0] = Output;
  //   Selector[3:0] = in_3
endmodule

module Program_Counter (
  input  [31:0] Input,
  input  clk,
  input  Load_PC,
  input  RST,
  output [31:0] Output
);

  Register #(.width(32)) PC (.D(Input), .en(Load_PC), .Q(Output), .clk(clk), .clr(RST));

  // Other names for the same wires on the sheet: LPC = Load_PC; PC_Out[31:0] = Output
endmodule

module Branch_Control (
  input  [31:0] PC,
  input  [31:0] RS,
  input  [15:0] offset,
  input  [25:0] destino,
  input  [2:0] selector,
  input  RS____RT,
  output [31:0] Output
);

  wire and_1_out, and_2_out, and_3_out, and_4_out, and_5_out, B_jump, beq, bgtz, blez, bltz, bne,
       comparator_1_eq, comparator_1_lt, j, jr, nop, RS___0, RS___0_t, RS____0;
  wire [1:0] jump;
  wire [31:0] branch, PC___4, PC____dest;
  wire [31:18] offset_t;

  Decoder #(.select(3), .enable("false")) decoder_1 (
    .out0(nop), .out1(beq), .out2(bne), .out3(blez), .out4(bgtz), .out5(bltz), .out6(j), .out7(jr),
    .sel(selector));
  Adder #(.width(32)) adder_1 (.a(32'h4), .b(PC), .out(PC___4));  // open: cin, cout
  assign offset_t = {{13{offset[15]}}, offset[15]};  // Bit_Extender bit_extender_1
  and and_1 (and_1_out, RS____RT, beq);
  and and_2 (and_2_out, ~RS____RT, bne);  // AND_Gate
  and and_3 (and_3_out, RS____0, blez);
  and and_4 (and_4_out, bgtz, RS___0_t);
  and and_5 (and_5_out, RS___0, bltz);
  jump_case jump_case_1 (.jump(destino), .PC(PC), .Output(PC____dest));
  or or_1 (B_jump, and_1_out, and_2_out, and_3_out, and_5_out, and_4_out);
  Comparator #(.width(32)) comparator_1 (
    .a(RS), .b({32{1'b0}}), .gt(RS___0_t), .eq(comparator_1_eq), .lt(comparator_1_lt));
  Comparator #(.width(32)) comparator_2 (.a(RS), .b({32{1'b0}}), .lt(RS___0));  // open: gt, eq
  Priority_Encoder #(.select(2)) priority_encoder_1 (
    .in0(nop), .in1(B_jump), .in2(j), .in3(jr), .out(jump), .en_in(1'b1));  // open: gs, en_out
  Adder #(.width(32)) adder_2 (.a(PC___4), .b({offset_t, offset, 2'b00}), .out(branch));  // open: cin, cout
  or or_2 (RS____0, comparator_1_eq, comparator_1_lt);
  Multiplexer #(.select(2), .width(32), .enable("false")) multiplexer_1 (
    .in0(PC___4), .in1(branch), .in2(PC____dest), .in3(RS), .out(Output), .sel(jump));

  // Other names for the same wires on the sheet: dest[25:0] = destino; off[15:0] = offset; offset_t[17:2] = offset;
  //   RS___RT = RS____RT
endmodule

module jump_case (
  input  [25:0] jump,
  input  [31:0] PC,
  output [31:0] Output
);


  assign Output = {PC[31:28], jump, 2'b00};
endmodule

module selector_branch (
  input  in_1,
  input  in_2,
  input  in_3,
  output [1:0] Output
);

  wire and_1_out, and_2_out, and_3_out;

  and and_1 (and_1_out, in_1, ~in_2, ~in_3);  // AND_Gate
  and and_2 (and_2_out, ~in_1, in_2, ~in_3);  // AND_Gate
  and and_3 (and_3_out, ~in_1, ~in_2, in_3);  // AND_Gate
  or or_1 (Output[0], and_1_out, and_2_out);
  or or_2 (Output[1], and_2_out, and_3_out);
endmodule
